// Logisim project computer.circ as structural Verilog: 2 circuits, main circuit computer
module computer (
  input  in_1
);

  wire cpu_1_writem;
  wire [14:0] cpu_1_addressm;
  wire [15:0] cpu_1_aluout, cpu_1_prc, rom_1_data, undriven;

  ROM #(.addrWidth(16), .dataWidth(16)) rom_1 (.addr(cpu_1_prc), .data(rom_1_data));
  CPU cpu_1 (
    .INSTRUCTION(rom_1_data), .inM(undriven), .RESET(in_1), .ALUout(cpu_1_aluout), .PRC(cpu_1_prc),
    .WriteM(cpu_1_writem), .AddressM(cpu_1_addressm));

  // Notes on the sheet:
  //   contents of rom_1 (hex, n*v repeats v):
  //   6fff ee88
endmodule

module SM (
  input  [14:0] address,
  input  CPUEnableWrite,
  output WriteToScreen,
  output SelKeyBoard,
  output [7:0] PY,
  output [8:0] PX
);

  wire and_1_out, comparator_1_eq, comparator_1_gt, not_1_out, or_1_out;
  wire [1:0] pull_resistor_1_node;
  wire [14:0] subtractor_1_out;

  or or_1 (or_1_out, comparator_1_gt, comparator_1_eq);
  Comparator #(.mode("unsigned"), .width(15)) comparator_1 (
    .a(address), .b(15'h4000), .gt(comparator_1_gt), .eq(comparator_1_eq));  // open: lt
  not not_1 (not_1_out, SelKeyBoard);
  Comparator #(.mode("unsigned"), .width(15)) comparator_2 (
    .a(address), .b(15'h6000), .eq(SelKeyBoard));  // open: gt, lt
  Subtractor #(.width(15)) subtractor_1 (.a(address), .b(15'h4000), .out(subtractor_1_out));  // open: bin, bout
  and and_1 (and_1_out, or_1_out, not_1_out);
  Pull_Resistor pull_resistor_1 (.node(pull_resistor_1_node));
  and and_2 (WriteToScreen, CPUEnableWrite, and_1_out);
  Shifter #(.width(17)) shifter_1 (.in({pull_resistor_1_node, subtractor_1_out}), .\dist (5'b00100), .out({PY, PX}));
endmodule
